// Logisim project B23CS1069.circ as structural Verilog: 6 circuits, main circuit main
module main (
  input  [31:0] INPUT1,
  input  [23:0] PC,
  input  [31:0] INPUT2,
  input  in_4,
  output [5:0] Current_OP_Code,
  output Zero,
  output [4:0] rs,
  output [4:0] rt,
  output [31:0] ALU_result,
  output [31:0] Current_Instruction,
  output [4:0] rd,
  output [31:0] CONSTANT_OFFSET,
  output [3:0] ALU_control,
  output [5:0] function_bits,
  output [1:0] ALUop
);

  ROM #(.addrWidth(24), .dataWidth(32)) rom_1 (.addr(PC), .data(Current_Instruction), .sel(in_4));
  assign CONSTANT_OFFSET = {{16{Current_Instruction[15]}}, Current_Instruction[15:0]};  // Bit_Extender bit_extender_1
  Control_Unit control_unit_1 (
    ._6_bit_opcode(Current_Instruction[31:26]), .ALUop10(ALUop));  // open: RegDst, Jump, Branch, MemRead, MemToReg, MemWrite, ALUsrc, RegWrite
  Hex_Digit_Display hex_digit_display_1 (.value(INPUT1[11:8]));  // open: dp
  Hex_Digit_Display hex_digit_display_2 (.value(INPUT1[3:0]));  // open: dp
  Hex_Digit_Display hex_digit_display_3 (.value(INPUT1[7:4]));  // open: dp
  ALU_Control alu_control_1 (.ALUop(ALUop), .Function_bits(Current_Instruction[5:0]), .out_3(ALU_control));
  Hex_Digit_Display hex_digit_display_4 (.value(INPUT2[11:8]));  // open: dp
  ALU_32 alu_32_1 (.in_1(INPUT1), .in_2(INPUT2), .out_4(Zero), .out_5(ALU_result), .in_3(ALU_control));
  Hex_Digit_Display hex_digit_display_5 (.value(INPUT2[7:4]));  // open: dp
  Hex_Digit_Display hex_digit_display_6 (.value(INPUT2[3:0]));  // open: dp
  Hex_Digit_Display hex_digit_display_7 (.value(ALU_result[7:4]));  // open: dp
  Hex_Digit_Display hex_digit_display_8 (.value(ALU_result[11:8]));  // open: dp
  Hex_Digit_Display hex_digit_display_9 (.value(ALU_result[3:0]));  // open: dp

  assign Current_OP_Code = Current_Instruction[31:26];
  assign function_bits = Current_Instruction[5:0];
  assign rd = Current_Instruction[15:11];
  assign rs = Current_Instruction[25:21];
  assign rt = Current_Instruction[20:16];

  // Notes on the sheet:
  //   ROM => load instance
  //   "./ROM_instances/test_instructions"
  //   contents of rom_1 (hex, n*v repeats v):
  //   2114024 2324825 2745020 2b65822 211602a 2326827 afa8ffec 8e090080 122a0019 8aaaaaa
endmodule

module ALU_32 (
  input  [31:0] in_1,
  input  [31:0] in_2,
  input  [3:0] in_3,
  output out_4,
  output [31:0] out_5
);

  wire comparator_1_lt;
  wire [31:0] adder_1_out, and_1_out, bit_extender_1_out, nor_1_out, or_1_out, subtractor_1_out;

  assign and_1_out = in_1 & in_2;  // AND_Gate and_1, 32 bits wide
  assign or_1_out = in_1 | in_2;  // OR_Gate or_1, 32 bits wide
  Adder #(.width(32)) adder_1 (.a(in_1), .b(in_2), .out(adder_1_out));  // open: cin, cout
  Subtractor #(.width(32)) subtractor_1 (.a(in_1), .b(in_2), .out(subtractor_1_out));  // open: bin, bout
  Comparator #(.width(32)) comparator_1 (.a(in_1), .b(in_2), .eq(out_4), .lt(comparator_1_lt));  // open: gt
  assign nor_1_out = ~(in_1 | in_2);  // NOR_Gate nor_1, 32 bits wide
  assign bit_extender_1_out = {{31{1'b0}}, comparator_1_lt};  // Bit_Extender bit_extender_1
  Multiplexer #(.select(4), .width(32)) multiplexer_1 (
    .in0(and_1_out), .in1(or_1_out), .in2(adder_1_out), .in6(subtractor_1_out), .in7(bit_extender_1_out),
    .in12(nor_1_out), .out(out_5), .sel(in_3), .en(1'b1));  // open: in3, in4, in5, in8, in9, in10, in11, in13, in14, in15

  // Notes on the sheet:
  //   msb
  //   lsb
  //   0000
  //   0001
  //   0010
  //   0110
  //   0111
  //   1100
endmodule

module Control_Unit (
  input  [5:0] _6_bit_opcode,
  output RegDst,
  output Jump,
  output Branch,
  output MemRead,
  output MemToReg,
  output [1:0] ALUop10,
  output MemWrite,
  output ALUsrc,
  output RegWrite
);

  Control_Unit_circuit control_unit_circuit_1 (
    .op5(_6_bit_opcode[5]), .op4(_6_bit_opcode[4]), .op3(_6_bit_opcode[3]), .op2(_6_bit_opcode[2]),
    .op1(_6_bit_opcode[1]), .op0(_6_bit_opcode[0]), .RegDst(RegDst), .Jump(Jump), .Branch(Branch),
    .MemRead(MemRead), .MemToReg(MemToReg), .ALUop1(ALUop10[1]), .ALUop0(ALUop10[0]), .MemWrite(MemWrite),
    .ALUsrc(ALUsrc), .RegWrite(RegWrite));
endmodule

module Control_Unit_circuit (
  input  op5,
  input  op4,
  input  op3,
  input  op2,
  input  op1,
  input  op0,
  output RegDst,
  output Jump,
  output Branch,
  output MemRead,
  output MemToReg,
  output ALUop1,
  output ALUop0,
  output MemWrite,
  output ALUsrc,
  output RegWrite
);

  wire not_1_out, not_2_out, not_3_out, not_4_out, not_5_out;

  not not_1 (not_1_out, op3);
  not not_2 (not_2_out, op2);
  not not_3 (not_3_out, op1);
  not not_4 (not_4_out, op3);
  not not_5 (not_5_out, op2);
  and and_1 (MemRead, not_1_out, op1);
  and and_2 (ALUop1, not_2_out, not_3_out);
  and and_3 (RegWrite, not_4_out, not_5_out);

  assign ALUop0 = op2;
  assign ALUsrc = op1;
  assign Branch = op2;
  assign Jump = 1'b0;
  assign MemToReg = op1;
  assign MemWrite = op3;
  assign RegDst = 1'b1;
endmodule

module ALU_Control (
  input  [1:0] ALUop,
  input  [5:0] Function_bits,
  output [3:0] out_3
);

  ALU_Control_circuit alu_control_circuit_1 (
    .ALUop1(ALUop[1]), .ALUop0(ALUop[0]), .func5(Function_bits[5]), .func4(Function_bits[4]),
    .func3(Function_bits[3]), .func2(Function_bits[2]), .func1(Function_bits[1]), .func0(Function_bits[0]),
    .AC3(out_3[3]), .AC2(out_3[2]), .AC1(out_3[1]), .AC0(out_3[0]));
endmodule

module ALU_Control_circuit (
  input  ALUop1,
  input  ALUop0,
  input  func5,
  input  func4,
  input  func3,
  input  func2,
  input  func1,
  input  func0,
  output AC3,
  output AC2,
  output AC1,
  output AC0
);

  wire and_1_out, and_2_out, and_3_out, and_4_out, and_5_out, and_6_out, and_7_out, and_8_out, and_9_out,
       and_10_out, not_1_out, not_2_out, not_3_out, not_4_out, not_5_out, not_6_out, not_7_out, not_8_out,
       not_9_out, not_10_out, not_11_out, not_12_out, not_13_out, not_14_out, not_15_out, not_16_out,
       not_17_out, not_18_out, not_19_out, not_20_out, not_21_out, not_22_out;

  not not_1 (not_1_out, ALUop0);
  not not_2 (not_2_out, func5);
  not not_3 (not_3_out, ALUop0);
  not not_4 (not_4_out, func4);
  not not_5 (not_5_out, func3);
  and and_1 (and_1_out, ALUop1, not_6_out);
  not not_6 (not_6_out, func5);
  and and_2 (and_2_out, ALUop1, func1);
  and and_3 (and_3_out, ALUop1, func3);
  and and_4 (and_4_out, ALUop1, func4);
  not not_7 (not_7_out, ALUop1);
  not not_8 (not_8_out, func5);
  not not_9 (not_9_out, func2);
  not not_10 (not_10_out, ALUop0);
  not not_11 (not_11_out, func5);
  not not_12 (not_12_out, ALUop0);
  not not_13 (not_13_out, func4);
  not not_14 (not_14_out, func3);
  not not_15 (not_15_out, func2);
  not not_16 (not_16_out, ALUop0);
  not not_17 (not_17_out, func4);
  not not_18 (not_18_out, func3);
  not not_19 (not_19_out, func1);
  not not_20 (not_20_out, ALUop0);
  not not_21 (not_21_out, func4);
  not not_22 (not_22_out, func0);
  and and_5 (and_5_out, ALUop1, not_1_out, not_2_out, func4, func3, func1, func0);
  and and_6 (and_6_out, ALUop1, not_3_out, func5, not_4_out, not_5_out, func2, func1, func0);
  or or_1 (AC2, ALUop0, and_1_out, and_2_out, and_3_out, and_4_out);
  or or_2 (AC1, not_7_out, not_8_out, not_9_out, func3, func4, ALUop0);
  and and_7 (and_7_out, ALUop1, not_10_out, not_11_out, func4, func3, func1, func0);
  and and_8 (and_8_out, ALUop1, not_12_out, func5, not_13_out, not_14_out, not_15_out, func0);
  and and_9 (and_9_out, ALUop1, not_16_out, func5, not_17_out, not_18_out, not_19_out, func0);
  and and_10 (and_10_out, ALUop1, not_20_out, func5, not_21_out, func3, not_22_out);
  or or_3 (AC3, and_5_out, and_6_out);
  or or_4 (AC0, and_7_out, and_8_out, and_9_out, and_10_out);
endmodule
