// Logisim project MIPS_processor.circ as structural Verilog: 9 circuits, main circuit main
module main (
  input  pause_execution,
  input  reset_PC_reg,
  input  [31:0] custom_PC,
  input  load_custom_PC,
  output [5:0] Current_OP_Code,
  output [31:0] Current_Instruction,
  output [31:0] CONSTANT_OFFSET,
  output [5:0] function_bits,
  output [1:0] ALUop,
  output [3:0] ALU_signal,
  output [31:0] ALU_result,
  output [4:0] read1_rs,
  output [4:0] read2_rt,
  output [4:0] write_rt_rd
);

  wire alu_32_1_out_4, and_1_out, clock_1_out, clock_2_out, clock_3_out, comparator_1_eq,
       control_unit_1_alusrc, control_unit_1_branch, control_unit_1_jump, control_unit_1_memread,
       control_unit_1_memtoreg, control_unit_1_memwrite, control_unit_1_regdst, control_unit_1_regwrite,
       keyboard_1_avail, not_1_out;
  wire [3:0] adder_1_out;
  wire [6:0] keyboard_1_data;
  wire [27:0] adder_1_out_2;
  wire [31:0] adder_2_out, data_memory_1_read_data, multiplexer_1_out, multiplexer_3_out, multiplexer_4_out,
       multiplexer_5_out, multiplexer_6_out, PC_reg_q, register_file_1_out_6, register_file_1_out_7,
       shifter_1_out;

  Clock clock_1 (.out(clock_1_out));
  Hex_Digit_Display hex_digit_display_1 (.value(PC_reg_q[31:28]));  // open: dp
  Hex_Digit_Display hex_digit_display_2 (.value(PC_reg_q[27:24]));  // open: dp
  Multiplexer #(.width(32)) multiplexer_1 (
    .in0(multiplexer_5_out), .in1(custom_PC), .out(multiplexer_1_out), .sel(load_custom_PC));
  not not_1 (not_1_out, pause_execution);
  Hex_Digit_Display hex_digit_display_3 (.value(PC_reg_q[23:20]));  // open: dp
  Hex_Digit_Display hex_digit_display_4 (.value(PC_reg_q[19:16]));  // open: dp
  Register #(.width(32)) PC_reg (
    .D(multiplexer_1_out), .en(not_1_out), .clk(clock_1_out), .Q(PC_reg_q), .clr(reset_PC_reg));
  Hex_Digit_Display hex_digit_display_5 (.value(PC_reg_q[15:12]));  // open: dp
  Hex_Digit_Display hex_digit_display_6 (.value(PC_reg_q[11:8]));  // open: dp
  Hex_Digit_Display hex_digit_display_7 (.value(PC_reg_q[7:4]));  // open: dp
  Hex_Digit_Display hex_digit_display_8 (.value(PC_reg_q[3:0]));  // open: dp
  Adder #(.width(32)) adder_1 (.a(PC_reg_q), .b(32'h4), .out({adder_1_out, adder_1_out_2}));  // open: cin, cout
  Instruction_Memory instruction_memory_1 (.Byte_address(PC_reg_q), .Data(Current_Instruction));
  Multiplexer #(.width(5)) multiplexer_2 (
    .in0(Current_Instruction[20:16]), .in1(Current_Instruction[15:11]), .out(write_rt_rd),
    .sel(control_unit_1_regdst));
  Control_Unit control_unit_1 (
    .opcode(Current_Instruction[31:26]), .Jump(control_unit_1_jump), .Branch(control_unit_1_branch),
    .MemRead(control_unit_1_memread), .MemToReg(control_unit_1_memtoreg), .ALUop10(ALUop),
    .MemWrite(control_unit_1_memwrite), .ALUsrc(control_unit_1_alusrc), .RegDst(control_unit_1_regdst),
    .RegWrite(control_unit_1_regwrite));
  assign CONSTANT_OFFSET = {{16{Current_Instruction[15]}}, Current_Instruction[15:0]};  // Bit_Extender bit_extender_1
  Register_File register_file_1 (
    .read_dest_2(Current_Instruction[20:16]), .read_dest_1(Current_Instruction[25:21]),
    .RegWrite(control_unit_1_regwrite), .write_dest(write_rt_rd), .Write_data_input(multiplexer_6_out),
    .out_7(register_file_1_out_7), .out_6(register_file_1_out_6));
  Shifter #(.width(32)) shifter_1 (.in(CONSTANT_OFFSET), .\dist (5'b00010), .out(shifter_1_out));
  Multiplexer #(.width(32)) multiplexer_3 (
    .in0(register_file_1_out_7), .in1(CONSTANT_OFFSET), .out(multiplexer_3_out), .sel(control_unit_1_alusrc));
  Adder #(.width(32)) adder_2 (
    .a({adder_1_out, adder_1_out_2}), .b(shifter_1_out), .out(adder_2_out));  // open: cin, cout
  ALU_Control alu_control_1 (.Function_bits(Current_Instruction[5:0]), .ALUop(ALUop), .out_3(ALU_signal));
  ALU_32 alu_32_1 (
    .in_1(register_file_1_out_6), .in_2(multiplexer_3_out), .in_3(ALU_signal), .out_5(ALU_result),
    .out_4(alu_32_1_out_4));
  Multiplexer #(.width(32)) multiplexer_4 (
    .in0({adder_1_out, adder_1_out_2}), .in1(adder_2_out), .out(multiplexer_4_out), .sel(and_1_out));
  and and_1 (and_1_out, control_unit_1_branch, alu_32_1_out_4);
  Multiplexer #(.width(32)) multiplexer_5 (
    .in0(multiplexer_4_out), .in1({adder_1_out, Current_Instruction[25:0], 2'b00}), .out(multiplexer_5_out),
    .sel(control_unit_1_jump));
  Data_Memory data_memory_1 (
    .memRead(control_unit_1_memread), .memWrite(control_unit_1_memwrite), .Byte_address(ALU_result),
    .Write_data(register_file_1_out_7), .Read_data(data_memory_1_read_data));
  Multiplexer #(.width(32)) multiplexer_6 (
    .in0(ALU_result), .in1(data_memory_1_read_data), .out(multiplexer_6_out), .sel(control_unit_1_memtoreg));
  Clock clock_2 (.out(clock_2_out));
  Keyboard keyboard_1 (
    .clk(clock_2_out), .re(keyboard_1_avail), .avail(keyboard_1_avail), .data(keyboard_1_data));  // open: clr
  Comparator #(.width(7)) comparator_1 (.a(keyboard_1_data), .b(7'b1000001), .eq(comparator_1_eq));  // open: gt, lt
  Clock clock_3 (.out(clock_3_out));
  TTY #(.cols(64), .rows(16)) tty_1 (
    .data(keyboard_1_data), .clk(clock_3_out), .we(keyboard_1_avail), .clr(comparator_1_eq));

  assign Current_OP_Code = Current_Instruction[31:26];
  assign function_bits = Current_Instruction[5:0];
  assign read1_rs = Current_Instruction[25:21];
  assign read2_rt = Current_Instruction[20:16];

  // Notes on the sheet:
  //   Instruction Byte Address (PC value)
endmodule

module ALU_32 (
  input  [31:0] in_1,
  input  [31:0] in_2,
  input  [3:0] in_3,
  output out_4,
  output [31:0] out_5
);

  wire comparator_1_lt;
  wire [31:0] adder_1_out, and_1_out, bit_extender_1_out, nor_1_out, or_1_out, subtractor_1_out;

  assign and_1_out = in_1 & in_2;  // AND_Gate and_1, 32 bits wide
  assign or_1_out = in_1 | in_2;  // OR_Gate or_1, 32 bits wide
  Adder #(.width(32)) adder_1 (.a(in_1), .b(in_2), .out(adder_1_out));  // open: cin, cout
  Subtractor #(.width(32)) subtractor_1 (.a(in_1), .b(in_2), .out(subtractor_1_out));  // open: bin, bout
  Comparator #(.width(32)) comparator_1 (.a(in_1), .b(in_2), .eq(out_4), .lt(comparator_1_lt));  // open: gt
  assign nor_1_out = ~(in_1 | in_2);  // NOR_Gate nor_1, 32 bits wide
  assign bit_extender_1_out = {{31{comparator_1_lt}}, comparator_1_lt};  // Bit_Extender bit_extender_1
  Multiplexer #(.select(4), .width(32)) multiplexer_1 (
    .in0(and_1_out), .in1(or_1_out), .in2(adder_1_out), .in6(subtractor_1_out), .in7(bit_extender_1_out),
    .in12(nor_1_out), .out(out_5), .sel(in_3));  // open: in3, in4, in5, in8, in9, in10, in11, in13, in14, in15

  // Notes on the sheet:
  //   msb
  //   lsb
  //   0000
  //   0001
  //   0010
  //   0110
  //   0111
  //   1100
endmodule

module Control_Unit (
  input  [5:0] opcode,
  output RegDst,
  output Jump,
  output Branch,
  output MemRead,
  output MemToReg,
  output [1:0] ALUop10,
  output MemWrite,
  output ALUsrc,
  output RegWrite
);

  Control_Unit_circuit control_unit_circuit_1 (
    .op5(opcode[5]), .op4(opcode[4]), .op3(opcode[3]), .op2(opcode[2]), .op1(opcode[1]), .op0(opcode[0]),
    .RegDst(RegDst), .Jump(Jump), .Branch(Branch), .MemRead(MemRead), .MemToReg(MemToReg),
    .ALUop1(ALUop10[1]), .ALUop0(ALUop10[0]), .MemWrite(MemWrite), .ALUsrc(ALUsrc), .RegWrite(RegWrite));
endmodule

module Control_Unit_circuit (
  input  op5,
  input  op4,
  input  op3,
  input  op2,
  input  op1,
  input  op0,
  output RegDst,
  output Jump,
  output Branch,
  output MemRead,
  output MemToReg,
  output ALUop1,
  output ALUop0,
  output MemWrite,
  output ALUsrc,
  output RegWrite
);

  wire and_4_out, and_5_out, not_1_out, not_2_out, not_4_out;

  not not_1 (not_1_out, op3);
  not not_2 (not_2_out, op2);
  not not_3 (RegDst, op1);
  not not_4 (not_4_out, op0);
  and and_1 (Jump, op1, not_4_out);
  and and_2 (MemRead, not_1_out, op0);
  and and_3 (ALUop1, not_2_out, RegDst);
  and and_4 (and_4_out, not_2_out, RegDst);
  or or_1 (RegWrite, and_4_out, and_5_out);
  and and_5 (and_5_out, not_1_out, op0);

  assign ALUop0 = op2;
  assign ALUsrc = op0;
  assign Branch = op2;
  assign MemToReg = op0;
  assign MemWrite = op3;
endmodule

module ALU_Control (
  input  [1:0] ALUop,
  input  [5:0] Function_bits,
  output [3:0] out_3
);

  ALU_Control_circuit alu_control_circuit_1 (
    .ALUop1(ALUop[1]), .ALUop0(ALUop[0]), .func5(Function_bits[5]), .func4(Function_bits[4]),
    .func3(Function_bits[3]), .func2(Function_bits[2]), .func1(Function_bits[1]), .func0(Function_bits[0]),
    .AC3(out_3[3]), .AC2(out_3[2]), .AC1(out_3[1]), .AC0(out_3[0]));
endmodule

module ALU_Control_circuit (
  input  ALUop1,
  input  ALUop0,
  input  func5,
  input  func4,
  input  func3,
  input  func2,
  input  func1,
  input  func0,
  output AC3,
  output AC2,
  output AC1,
  output AC0
);

  wire and_1_out, and_2_out, and_3_out, and_4_out, and_5_out, and_6_out, and_7_out, and_8_out, and_9_out,
       and_10_out, not_1_out, not_2_out, not_3_out, not_4_out, not_5_out, not_6_out, not_7_out, not_8_out,
       not_9_out, not_10_out, not_11_out, not_12_out, not_13_out, not_14_out, not_15_out, not_16_out,
       not_17_out, not_18_out, not_19_out, not_20_out, not_21_out, not_22_out;

  not not_1 (not_1_out, ALUop0);
  not not_2 (not_2_out, func5);
  not not_3 (not_3_out, ALUop0);
  not not_4 (not_4_out, func4);
  not not_5 (not_5_out, func3);
  and and_1 (and_1_out, ALUop1, not_6_out);
  not not_6 (not_6_out, func5);
  and and_2 (and_2_out, ALUop1, func1);
  and and_3 (and_3_out, ALUop1, func3);
  and and_4 (and_4_out, ALUop1, func4);
  not not_7 (not_7_out, ALUop1);
  not not_8 (not_8_out, func5);
  not not_9 (not_9_out, func2);
  not not_10 (not_10_out, ALUop0);
  not not_11 (not_11_out, func5);
  not not_12 (not_12_out, ALUop0);
  not not_13 (not_13_out, func4);
  not not_14 (not_14_out, func3);
  not not_15 (not_15_out, func2);
  not not_16 (not_16_out, ALUop0);
  not not_17 (not_17_out, func4);
  not not_18 (not_18_out, func3);
  not not_19 (not_19_out, func1);
  not not_20 (not_20_out, ALUop0);
  not not_21 (not_21_out, func4);
  not not_22 (not_22_out, func0);
  and and_5 (and_5_out, ALUop1, not_1_out, not_2_out, func4, func3, func1, func0);
  and and_6 (and_6_out, ALUop1, not_3_out, func5, not_4_out, not_5_out, func2, func1, func0);
  or or_1 (AC2, and_1_out, and_3_out);
  or or_2 (AC1, not_7_out, not_8_out, not_9_out, func3, func4, ALUop0);
  and and_7 (and_7_out, ALUop1, not_10_out, not_11_out, func4, func3, func1, func0);
  and and_8 (and_8_out, ALUop1, not_12_out, func5, not_13_out, not_14_out, not_15_out, func0);
  and and_9 (and_9_out, ALUop1, not_16_out, func5, not_17_out, not_18_out, not_19_out, func0);
  and and_10 (and_10_out, ALUop1, not_20_out, func5, not_21_out, func3, not_22_out);
  or or_3 (AC3, and_5_out, and_6_out);
  or or_4 (AC0, and_7_out, and_8_out, and_9_out, and_10_out);
endmodule

module Register_File (
  input  RegWrite,
  input  [4:0] write_dest,
  input  [4:0] read_dest_1,
  input  [31:0] Write_data_input,
  input  [4:0] read_dest_2,
  output [31:0] out_6,
  output [31:0] out_7
);

  wire clock_1_out, demultiplexer_1_out1, demultiplexer_1_out2, demultiplexer_1_out3, demultiplexer_1_out4,
       demultiplexer_1_out5, demultiplexer_1_out6, demultiplexer_1_out7, demultiplexer_1_out8,
       demultiplexer_1_out9, demultiplexer_1_out10, demultiplexer_1_out11, demultiplexer_1_out12,
       demultiplexer_1_out13, demultiplexer_1_out14, demultiplexer_1_out15, w17, w18, w19, w20, w21, w22,
       w23, w24, w25, w26, w27, w28, w29, w30, w31, w32;
  wire [4:0] and_1_out, bit_extender_1_out;
  wire [31:0] r1, r2, r3, r4, r5, r6, r7, r8, r9, r10, r11, r12, r13, r14, r15, r16, r17, r18, r19, r20, r21,
       r22, r23, r24, r25, r26, r27, r28, r29, r30, r31, r32;

  Clock clock_1 (.out(clock_1_out));
  assign bit_extender_1_out = {{4{RegWrite}}, RegWrite};  // Bit_Extender bit_extender_1
  Demultiplexer #(.enable("true"), .select(5)) demultiplexer_1 (
    .out1(demultiplexer_1_out1), .out2(demultiplexer_1_out2), .out3(demultiplexer_1_out3),
    .out4(demultiplexer_1_out4), .out5(demultiplexer_1_out5), .out6(demultiplexer_1_out6),
    .out7(demultiplexer_1_out7), .out8(demultiplexer_1_out8), .out9(demultiplexer_1_out9),
    .out10(demultiplexer_1_out10), .out11(demultiplexer_1_out11), .out12(demultiplexer_1_out12),
    .out13(demultiplexer_1_out13), .out14(demultiplexer_1_out14), .out15(demultiplexer_1_out15), .out16(w17),
    .out17(w18), .out18(w19), .out19(w20), .out20(w21), .out21(w22), .out22(w23), .out23(w24), .out24(w25),
    .out25(w26), .out26(w27), .out27(w28), .out28(w29), .out29(w30), .out30(w31), .out31(w32), .in(1'b1),
    .sel(and_1_out), .en(1'b1));  // open: out0
  assign and_1_out = bit_extender_1_out & write_dest;  // AND_Gate and_1, 5 bits wide
  Register #(.width(32)) register_1 (
    .D(Write_data_input), .en(demultiplexer_1_out8), .Q(r9), .clk(clock_1_out), .clr(1'b0));
  Register #(.width(32)) register_2 (
    .D(Write_data_input), .en(demultiplexer_1_out9), .Q(r10), .clk(clock_1_out), .clr(1'b0));
  Register #(.width(32)) register_3 (
    .D(Write_data_input), .en(demultiplexer_1_out10), .Q(r11), .clk(clock_1_out), .clr(1'b0));
  Register #(.width(32)) register_4 (
    .D(Write_data_input), .en(demultiplexer_1_out11), .Q(r12), .clk(clock_1_out), .clr(1'b0));
  Register #(.width(32)) register_5 (
    .D(Write_data_input), .en(demultiplexer_1_out12), .Q(r13), .clk(clock_1_out), .clr(1'b0));
  Register #(.width(32)) register_6 (
    .D(Write_data_input), .en(demultiplexer_1_out13), .Q(r14), .clk(clock_1_out), .clr(1'b0));
  Register #(.width(32)) register_7 (
    .D(Write_data_input), .en(demultiplexer_1_out14), .Q(r15), .clk(clock_1_out), .clr(1'b0));
  Register #(.width(32)) register_8 (
    .D(Write_data_input), .en(demultiplexer_1_out15), .Q(r16), .clk(clock_1_out), .clr(1'b0));
  Register #(.width(32)) zero (.en(1'b0), .Q(r1), .clr(1'b1));  // open: D, clk
  Register #(.width(32)) register_9 (
    .D(Write_data_input), .en(demultiplexer_1_out1), .Q(r2), .clk(clock_1_out), .clr(1'b0));
  Register #(.width(32)) register_10 (
    .D(Write_data_input), .en(demultiplexer_1_out2), .Q(r3), .clk(clock_1_out), .clr(1'b0));
  Register #(.width(32)) register_11 (
    .D(Write_data_input), .en(demultiplexer_1_out3), .Q(r4), .clk(clock_1_out), .clr(1'b0));
  Register #(.width(32)) register_12 (
    .D(Write_data_input), .en(demultiplexer_1_out4), .Q(r5), .clk(clock_1_out), .clr(1'b0));
  Register #(.width(32)) register_13 (
    .D(Write_data_input), .en(demultiplexer_1_out5), .Q(r6), .clk(clock_1_out), .clr(1'b0));
  Register #(.width(32)) register_14 (
    .D(Write_data_input), .en(demultiplexer_1_out6), .Q(r7), .clk(clock_1_out), .clr(1'b0));
  Register #(.width(32)) register_15 (
    .D(Write_data_input), .en(demultiplexer_1_out7), .Q(r8), .clk(clock_1_out), .clr(1'b0));
  Register #(.width(32)) register_16 (.D(Write_data_input), .en(w17), .Q(r17), .clk(clock_1_out), .clr(1'b0));
  Register #(.width(32)) register_17 (.D(Write_data_input), .en(w18), .Q(r18), .clk(clock_1_out), .clr(1'b0));
  Register #(.width(32)) register_18 (.D(Write_data_input), .en(w19), .Q(r19), .clk(clock_1_out), .clr(1'b0));
  Register #(.width(32)) register_19 (.D(Write_data_input), .en(w20), .Q(r20), .clk(clock_1_out), .clr(1'b0));
  Register #(.width(32)) register_20 (.D(Write_data_input), .en(w21), .Q(r21), .clk(clock_1_out), .clr(1'b0));
  Register #(.width(32)) register_21 (.D(Write_data_input), .en(w22), .Q(r22), .clk(clock_1_out), .clr(1'b0));
  Register #(.width(32)) register_22 (.D(Write_data_input), .en(w23), .Q(r23), .clk(clock_1_out), .clr(1'b0));
  Register #(.width(32)) register_23 (.D(Write_data_input), .en(w24), .Q(r24), .clk(clock_1_out), .clr(1'b0));
  Register #(.width(32)) register_24 (.D(Write_data_input), .en(w25), .Q(r25), .clk(clock_1_out), .clr(1'b0));
  Register #(.width(32)) register_25 (.D(Write_data_input), .en(w26), .Q(r26), .clk(clock_1_out), .clr(1'b0));
  Register #(.width(32)) register_26 (.D(Write_data_input), .en(w27), .Q(r27), .clk(clock_1_out), .clr(1'b0));
  Register #(.width(32)) register_27 (.D(Write_data_input), .en(w28), .Q(r28), .clk(clock_1_out), .clr(1'b0));
  Register #(.width(32)) register_28 (.D(Write_data_input), .en(w29), .Q(r29), .clk(clock_1_out), .clr(1'b0));
  Register #(.width(32)) register_29 (.D(Write_data_input), .en(w30), .Q(r30), .clk(clock_1_out), .clr(1'b0));
  Register #(.width(32)) register_30 (.D(Write_data_input), .en(w31), .Q(r31), .clk(clock_1_out), .clr(1'b0));
  Register #(.width(32)) register_31 (.D(Write_data_input), .en(w32), .Q(r32), .clk(clock_1_out), .clr(1'b0));
  Multiplexer #(.enable("true"), .select(5), .width(32)) multiplexer_1 (
    .in0(r1), .in1(r2), .in2(r3), .in3(r4), .in4(r5), .in5(r6), .in6(r7), .in7(r8), .in8(r9), .in9(r10),
    .in10(r11), .in11(r12), .in12(r13), .in13(r14), .in14(r15), .in15(r16), .in16(r17), .in17(r18),
    .in18(r19), .in19(r20), .in20(r21), .in21(r22), .in22(r23), .in23(r24), .in24(r25), .in25(r26),
    .in26(r27), .in27(r28), .in28(r29), .in29(r30), .in30(r31), .in31(r32), .out(out_6), .sel(read_dest_1),
    .en(1'b1));
  Multiplexer #(.enable("true"), .select(5), .width(32)) multiplexer_2 (
    .in0(r1), .in1(r2), .in2(r3), .in3(r4), .in4(r5), .in5(r6), .in6(r7), .in7(r8), .in8(r9), .in9(r10),
    .in10(r11), .in11(r12), .in12(r13), .in13(r14), .in14(r15), .in15(r16), .in16(r17), .in17(r18),
    .in18(r19), .in19(r20), .in20(r21), .in21(r22), .in22(r23), .in23(r24), .in24(r25), .in25(r26),
    .in26(r27), .in27(r28), .in28(r29), .in29(r30), .in30(r31), .in31(r32), .out(out_7), .sel(read_dest_2),
    .en(1'b1));
endmodule

module Instruction_Memory (
  input  [31:0] Byte_address,
  output [31:0] Data
);

  wire [23:0] bit_extender_1_out;
  wire [31:0] shifter_1_out;

  Shifter #(.shift("lr"), .width(32)) shifter_1 (.in(Byte_address), .\dist (5'b00010), .out(shifter_1_out));
  Bit_Extender #(.in_width(32), .out_width(24)) bit_extender_1 (.in(shifter_1_out), .out(bit_extender_1_out));
  ROM #(.addrWidth(24), .dataWidth(32)) rom_1 (.addr(bit_extender_1_out), .data(Data));

  // Notes on the sheet:
  //   contents of rom_1 (hex, n*v repeats v):
  //   8c110000 8c120004 232402a 11000002 2324820 8000007 2324822 ac090008 8000008
endmodule

module Data_Memory (
  input  memRead,
  input  memWrite,
  input  [31:0] Byte_address,
  input  [31:0] Write_data,
  output [31:0] Read_data
);

  wire [23:0] bit_extender_1_out;
  wire [31:0] shifter_1_out;

  Shifter #(.shift("lr"), .width(32)) shifter_1 (.in(Byte_address), .\dist (5'b00010), .out(shifter_1_out));
  Bit_Extender #(.in_width(32), .out_width(24)) bit_extender_1 (.in(shifter_1_out), .out(bit_extender_1_out));
  RAM #(.addrWidth(24), .dataWidth(32), .trigger("high")) ram_1 (
    .addr(bit_extender_1_out), .we(memWrite), .oe(memRead), .din(Write_data), .dout(Read_data));
  Clock clock_1 ();  // open: out

  // Notes on the sheet:
  //   This is word addressable now, not byte addressable
  //   Converting byte address into word address
endmodule
